// Logisim project elevator_function.circ as structural Verilog: 1 circuit, main circuit main
module main (
  input  User_enable___1,
  input  Initialize,
  input  in_3,
  input  in_4,
  input  in_5,
  input  in_6,
  input  in_7,
  input  in_8,
  input  in_9
);

  wire and_1_out, and_2_out, and_3_out, and_4_out, and_5_out, and_6_out, and_7_out, clock_1_out, clock_2_out,
       clock_3_out, clock_4_out, counter_1_carry, d_ff_1_q, d_ff_2_q, d_ff_3_q, d_ff_4_q, not_1_out,
       not_2_out, not_3_out, not_4_out, not_5_out, not_6_out, not_7_out, not_8_out, not_9_out, not_10_out,
       not_11_out, not_12_out, not_13_out, or_1_out, or_2_out, or_3_out, or_4_out, t_ff_1_q, t_ff_2_q,
       t_ff_3_q;

  Clock clock_1 (.out(clock_1_out));
  D_Flip_Flop d_ff_1 (
    .clk(clock_1_out), .D(User_enable___1), .Q(d_ff_1_q), .en(not_1_out), .reset(Initialize));  // open: Qn, preset
  not not_1 (not_1_out, in_3);
  Clock clock_2 (.out(clock_2_out));
  Clock clock_3 (.out(clock_3_out));
  not not_2 (not_2_out, t_ff_3_q);
  and and_1 (and_1_out, d_ff_1_q, not_2_out, not_4_out, counter_1_carry);
  not not_3 (not_3_out, and_1_out);
  and and_2 (and_2_out, counter_1_carry, clock_2_out);
  and and_3 (and_3_out, not_7_out, t_ff_2_q, counter_1_carry);
  and and_4 (and_4_out, counter_1_carry, clock_3_out);
  and and_5 (and_5_out, not_7_out, t_ff_3_q, counter_1_carry, not_9_out);
  not not_4 (not_4_out, t_ff_2_q);
  and and_6 (and_6_out, counter_1_carry, clock_4_out);
  not not_5 (not_5_out, d_ff_2_q);
  D_Flip_Flop d_ff_2 (
    .clk(and_6_out), .D(not_3_out), .Q(d_ff_2_q), .en(not_6_out), .reset(Initialize));  // open: Qn, preset
  not not_6 (not_6_out, in_5);
  not not_7 (not_7_out, not_5_out);
  LED led_1 (.in(d_ff_3_q));
  D_Flip_Flop d_ff_3 (
    .clk(and_2_out), .D(and_3_out), .Q(d_ff_3_q), .en(not_8_out), .reset(Initialize));  // open: Qn, preset
  not not_8 (not_8_out, in_7);
  not not_9 (not_9_out, d_ff_3_q);
  LED led_2 (.in(d_ff_4_q));
  D_Flip_Flop d_ff_4 (
    .clk(and_4_out), .D(and_5_out), .Q(d_ff_4_q), .en(not_10_out), .reset(Initialize));  // open: Qn, preset
  not not_10 (not_10_out, in_9);
  LED led_3 (.in(not_5_out));
  or or_1 (or_1_out, not_5_out, d_ff_3_q);
  or or_2 (or_2_out, not_5_out, d_ff_4_q);
  LED led_4 (.in(or_2_out));
  Clock clock_4 (.out(clock_4_out));
  or or_3 (or_3_out, d_ff_4_q, or_1_out);
  or or_4 (or_4_out, d_ff_3_q, d_ff_4_q);
  not not_11 (not_11_out, in_8);
  LED led_5 (.in(d_ff_3_q));
  and and_7 (and_7_out, clock_4_out, or_3_out);
  T_Flip_Flop t_ff_1 (
    .clk(d_ff_4_q), .T(not_11_out), .Q(t_ff_1_q), .reset(Initialize), .en(not_11_out));  // open: Qn, preset
  LED led_6 (.in(t_ff_1_q));
  Counter #(.width(4), .max('hf)) counter_1 (.carry(counter_1_carry), .clk(and_7_out));  // open: load, D, count, Q, clr
  T_Flip_Flop t_ff_2 (
    .clk(or_1_out), .T(not_12_out), .Q(t_ff_2_q), .reset(Initialize), .en(not_12_out));  // open: Qn, preset
  not not_12 (not_12_out, in_4);
  T_Flip_Flop t_ff_3 (
    .clk(or_4_out), .T(not_13_out), .Q(t_ff_3_q), .reset(Initialize), .en(not_13_out));  // open: Qn, preset
  not not_13 (not_13_out, in_6);
  LED led_7 (.in(counter_1_carry));
  LED led_8 (.in(t_ff_2_q));
  LED led_9 (.in(t_ff_3_q));

  // Notes on the sheet:
  //   Door_A
  //   Move
  //   Door_B
  //   Door open=on, close=off
  //   Moving=on, stop=off
  //   Floor 1st=on, 2nd=off
  //   Counter
endmodule
